# Fritzing sketch prototipo (saved by Fritzing 0.9.3b)
breadboards: 1

parts:
  Componente1 = Adafruit ADS1115 16Bit I2C ADC [part_number="Adafruit #1085"]
  M1 = ESP32-S3-DevKitC-1-N8R8-v1 [part_number=ESP32-S3-DevKitC-1-N8R8-v1]
  Componente2 = ACS712 Current Sensor 5A 20A 30A
  Mod1 = zmpt101b
  LCD1 = TFT 1.8 inch 160x128 w SD
  KY-1 = Keyes Relay [package=THT]
  M2 = HLK-5M05

nets:
  N1: Componente1.AIN1, Componente2.2, Componente2.OUT
  N2: Componente1.AIN0, Mod1.OUT
  N3: Componente1.SDA, M1.pin_12
  N4: Componente1.SCL, M1.pin_15
  GND: Componente1.GND, Componente2.GND, Mod1.GND, M2.-Vo
  VCC: Componente1.VDD, Componente2.VCC, Mod1.VCC, M2.+Vo
  N5: M1.pin_1, M1.pin_2, LCD1.pin_1
  N6: M1.pin_5, LCD1.pin4
  N7: M1.pin_6, LCD1.pin_5
  N8: M1.pin_9, LCD1.pin_8
  N9: M1.pin_16, LCD1.pin3
  N10: M1.pin_17, LCD1.pin_6
  N11: M1.pin_18, LCD1.pin_7
  N12: M1.pin_19, KY-1.power
  N13: M1.pin_20, M1.pin_21, KY-1.signal
  N14: M1.pin_22, M1.pin_44, LCD1.pin2, KY-1.ground

custom parts:
  Adafruit ADS1115 16Bit I2C ADC: For microcontrollers without an analog-to-digital converter or when you want a higher-precision ADC, the ADS1115 provides 16-bit precision at 860 samples/second over I2C. The chip can be configured as 4 single-ended input channels, or two differential channels. As a nice bonus, it even includes a programmable gain amplifier, up to x16, to help boost up smaller single/differential signals to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
  ESP32-S3-DevKitC-1-N8R8-v1: ESP32-S3-DevKitC-1-N8R8-v1 This module is 44pins long (2x22) and 11 pins width.
  ACS712 Current Sensor 5A 20A 30A: Remix by Michael Kubina http://www.kubina.info Original by: https://forum.fritzing.org/t/current-sensor-5a-acs712/7694 https://forum.fritzing.org/u/ArtHome ArtHome12@gmail.com
  zmpt101b: Single phase ac active output voltate transformer module.
  TFT 1.8 inch 160x128 w SD: This is a generic 1.8 tft spi lcd display available on ebay and others. The 1.8" display has 128x160 color pixels.
  Keyes Relay: The Keyes 5V relay module is suitable for SCM development, home appliance control. It uses a 5V~12V TIL control signal which can control DC / AC signal.
  HLK-5M05: AC-DC 220V to 5V Step-Down Power Supply Module
